// Digital circuit ALU.dig as structural Verilog
module ALU (
  input  [7:0] A,
  input  [7:0] B,
  input  EO,
  input  SU,
  output [7:0] OP,
  output CY,
  output Z,
  output [7:0] DBG
);

  wire add_1_c_o, sub_1_c_o;
  wire [7:0] add_1_s, sub_1_s;

  Add #(.Bits(8), .generic("this.Bits=int(args.bitWidth);")) add_1 (
    .a(A), .b(B), .c_i(1'b0), .s(add_1_s), .c_o(add_1_c_o));
  Sub #(.Bits(8), .generic("this.Bits=int(args.bitWidth);")) sub_1 (
    .a(A), .b(B), .c_i(1'b0), .s(sub_1_s), .c_o(sub_1_c_o));
  Multiplexer #(.Bits(8), .generic("this.Bits=int(args.bitWidth);")) multiplexer_1 (
    .sel(SU), .in_0(add_1_s), .in_1(sub_1_s), .out(DBG));
  Multiplexer multiplexer_2 (.sel(SU), .in_0(add_1_c_o), .in_1(sub_1_c_o), .out(CY));
  assign OP = EO ? DBG : 8'bz;  // Driver driver_1
  Comparator #(.Bits(8)) comparator_1 (.a(DBG), .b({8{1'b0}}), .eq(Z));  // open: gt, lt

  // Notes on the sheet:
  //   A: First Input to ALU
  //   B: Second Input to ALU
  //   EO: Sum Out: outputs result of ALU operation to Bus when this signal is asserted
  //   SU: ALU will subtract when this signal is asserted, otherwise addition
  //   OP: Result of the ALU Operation
  //   CY: Carry flag for the ALU operation
  //   Z: The Zero flag (when ALU result is zero)
  //   DBG: Unbuffered output for debugging
endmodule
