// Digital circuit CLK.dig as structural Verilog
module CLK (
  input  C,
  input  HLT,
  output CLK
);

  wire not_1_out;

  and and_1 (CLK, C, not_1_out);
  not not_1 (not_1_out, HLT);

  // Notes on the sheet:
  //   HLT: CPU will halt when HIGH
  //   CLK: CPU Clock for all sub-units that need a clock
endmodule
