// Digital circuit CPU.dig as structural Verilog
module CPU (
  input  clk,
  input  MANUAL,
  input  HLT,
  input  MI,
  input  RI,
  input  RO,
  input  IO,
  input  II,
  input  AI,
  input  AO,
  input  EO,
  input  SU,
  input  BI,
  input  OI,
  input  CE,
  input  CO,
  input  J,
  input  FC,
  input  NI,
  output [7:0] DISPLAY,
  output [7:0] PC_DBG,
  output [7:0] A_DBG,
  output [7:0] B_DBG,
  output [7:0] IR_DBG,
  output [7:0] ALU_DBG,
  output [3:0] MAR_DBG
);

  wire AI_t, AO_t, B6, BI_t, CE_t, CF, CLK_t, CO_t, CY, Decoder_for_Jump_Control_y, EO_t, FC_t, HLT_t, II_t,
       IO_t, J_t, MI_t, NI_t, OI_t, reset_1_out, RI_t, RO_t, SU_t, Z, ZF;
  wire [2:0] counter_1_out, Instruction_Register_i;
  wire [7:0] eepromdualport_1_d;
  wire [16:0] Decoder_ROM_d;

  Reset reset_1 (.out(reset_1_out));
  Counter #(.Bits(3)) counter_1 (.en(reset_1_out), .C(~CLK_t), .clr(NI_t), .out(counter_1_out));  // open: ovf
  MAR MAR (.D(eepromdualport_1_d), .C(CLK_t), .MI(MI_t), .ADDR(MAR_DBG));
  EEPROMDualPort #(.AddrBits(4), .Bits(8)) eepromdualport_1 (
    .A(MAR_DBG), .Din(eepromdualport_1_d), .str(RI_t), .C(CLK_t), .ld(RO_t), .D(eepromdualport_1_d));
  IR #(.generic("BusWidth := 8;")) Instruction_Register (
    .Di(eepromdualport_1_d), .C(CLK_t), .LOAD(II_t), .ENABLE(IO_t), .ADDR(eepromdualport_1_d),
    .I({B6, Instruction_Register_i}), .DBG(IR_DBG));
  ROM #(.AddrBits(7), .Bits(17)) Decoder_ROM (
    .A({B6, Instruction_Register_i, counter_1_out}), .sel(1'b1), .D(Decoder_ROM_d));
  CLK System_Clock (.C(clk), .HLT(HLT_t), .CLK(CLK_t));
  Multiplexer #(.Bits(17)) multiplexer_1 (
    .sel(MANUAL), .in_0(Decoder_ROM_d),
    .in_1({NI, HLT, MI, RI, RO, IO, II, AI, AO, EO, SU, BI, OI, CE, CO, J, FC}),
    .out({NI_t, HLT_t, MI_t, RI_t, RO_t, IO_t, II_t, AI_t, AO_t, EO_t, SU_t, BI_t, OI_t, CE_t, CO_t, J_t, FC_t}));
  Reg #(.generic("BusWidth := 8;")) OUTPUT (
    .Di(eepromdualport_1_d), .LOAD(OI_t), .C(CLK_t), .ENABLE(1'b1), .Do(DISPLAY));  // open: Du
  PC Program_Counter (
    .CE(CE_t), .C(CLK_t), .PCi(eepromdualport_1_d), .CO(CO_t), .J(Decoder_for_Jump_Control_y), .DBG(PC_DBG),
    .PCo(eepromdualport_1_d));
  Reg #(.generic("BusWidth := 8;")) Reg_A (
    .Di(eepromdualport_1_d), .LOAD(AI_t), .C(CLK_t), .ENABLE(AO_t), .Du(A_DBG), .Do(eepromdualport_1_d));
  ALU #(.generic("bitWidth := 8;")) ALU (
    .A(A_DBG), .B(B_DBG), .EO(EO_t), .SU(SU_t), .OP(eepromdualport_1_d), .CY(CY), .Z(Z), .DBG(ALU_DBG));
  Reg #(.generic("BusWidth := 8;")) Reg_B (
    .Di(eepromdualport_1_d), .LOAD(BI_t), .C(CLK_t), .ENABLE(1'b1), .Du(B_DBG));  // open: Do
  Flag Flags_Register (.CYi(CY), .CLK(CLK_t), .FI(EO_t), .Zi(Z), .CYo(CF), .Zo(ZF));
  FlagsDecoder Decoder_for_Jump_Control (.J(J_t), .FC(FC_t), .B6(B6), .C(CF), .Z(ZF), .Y(Decoder_for_Jump_Control_y));

  // Notes on the sheet:
  //   clk: Hz: 500
  //   contents of eepromdualport_1 (hex, n*v repeats v):
  //   e0,2f,74,60,3f,e0,80,64,0,0,0,0,0,0,0,1
  //   contents of Decoder_ROM (hex, n*v repeats v):
  //   4004,1408,0,0,0,0,0,0,4004,1408,4800,11200,0,0,0,0,4004,1408,4800,1020,10280,0,0,
  //   0,4004,1408,4800,1020,102c0,0,0,0,4004,1408,4800,12100,0,0,0,0,4004,1408,10a00,0,
  //   0,0,0,0,4004,1408,10802,0,0,0,0,0,4004,1408,10803,0,0,0,0,0,4004,1408,10803,0,0,0,
  //   0,0,0,0,0,0,0,0,0,0,0,0,0,0,0,0,0,0,0,0,0,0,0,0,0,0,0,0,0,0,0,0,0,0,0,0,0,0,0,0,0,
  //   0,4004,1408,10110,0,0,0,0,0,4004,1408,18000,0,0,0,0,0,0,0,0,0,0,0,0,0,0,0,0,0,0,0,
  //   0,0,0,0,0,0,0,0,0,0,0,0,0,0,0,0,0,0,0,0,0,0,0,0,0,0,0,0,0,0,0,0,0,0,0,0,0,0,0,0,0,
  //   0,0,0,802,0,0,0,0,0,0,0,0,0,0,0,0,0,0,0,0,0,0,0,0,0,0,0,0,0,0,0,0,0,0,0,0,0,0,0,0,
  //   0,0,0,0,0,0,0,0,0,0,0,0,0,0,0,0,0,0,0,0,0,0,0,0,0,0,0,0,0,0,0,0,0,0,0,0,0,0,0,0,0,
  //   0,0,0,0,0,0,0,0,0,0,0,0,0,0,0,0,0,0,0,0,0,0,0,0,0,0,0,0,0,0,0,0,0,0,0,0,0,0,0,0,0,
  //   0,0,0,0,0,0,0,0,0,0,0,0,0,0,0,0,0,802
endmodule
