// Digital circuit Flag.dig as structural Verilog
module Flag (
  input  CYi,
  input  CLK,
  input  FI,
  input  Zi,
  output CYo,
  output Zo
);

  Register register_1 (.D(CYi), .C(CLK), .en(FI), .Q(CYo));
  Register register_2 (.D(Zi), .C(CLK), .en(FI), .Q(Zo));

  // Notes on the sheet:
  //   CYi: Carry Flag value to be stored in Flag Register
  //   FI: The flag is stored when this signal is asserted
  //   CYo: Carry Flag
  //   Zi: Zero Flag value to be stored in Flag Register
  //   Zo: Zero Flag
endmodule
