// Digital circuit FlagsDecoder.dig as structural Verilog
module FlagsDecoder (
  input  J,
  input  FC,
  input  B6,
  input  C,
  input  Z,
  output Y
);

  wire and_1_out, and_2_out, and_3_out, not_1_out, not_2_out;

  not not_1 (not_1_out, FC);
  not not_2 (not_2_out, B6);
  and and_1 (and_1_out, B6, J, Z);
  and and_2 (and_2_out, not_2_out, C, J);
  and and_3 (and_3_out, not_1_out, J);
  or or_1 (Y, and_1_out, and_2_out, and_3_out);

  // Notes on the sheet:
  //   Y: Decoded output
  //   J: Jump Flag
  //   FC: Flag Check
  //   B6: Highest bit of 7 bit micro-code instruction (B6)
  //   C: Carry Flag
  //   Z: Zero Flag
endmodule
