// Digital circuit IR.dig as structural Verilog
module IR (
  input  [7:0] Di,
  input  C,
  input  LOAD,
  input  ENABLE,
  output [7:0] ADDR,
  output [3:0] I,
  output [7:0] DBG
);

  Register #(.Bits(8), .generic("this.Bits=int(args.BusWidth);")) register_1 (.D(Di), .C(C), .en(LOAD), .Q(DBG));
  assign ADDR = ENABLE ? {4'b0000, DBG[3:0]} : 8'bz;  // Driver driver_1

  assign I = DBG[7:4];

  // Notes on the sheet:
  //   Di: Data to be stored in Register. Data is stored when LOAD is LOW and rising edge of CLK
  //   ADDR: The Address part (LSN) of the Instruction, adjusted back to 8 bits by setting higher bits to zero
  //   LOAD: Data is saved in register from bus when this signal is  asserted
  //   ENABLE: Register data output to bus when this signal is asserted
  //   I: The Instruction Code (HSN) of the instruction
  //   DBG: Unbuffered output for debugging
endmodule
