// Digital circuit MAR.dig as structural Verilog
module MAR (
  input  [7:0] D,
  input  C,
  input  MI,
  output [3:0] ADDR
);

  Register #(.Bits(4)) MAR (.D(D[3:0]), .C(C), .en(MI), .Q(ADDR));

  // Notes on the sheet:
  //   D: Instruction from system bus. Only the least significant nibble (LSN) is used for memory access
  //   MI: loads MAR from bus when this signal is asserted
  //   ADDR: The memory address to be used for memory access from RAM
endmodule
