// Digital circuit PC.dig as structural Verilog
module PC (
  input  CE,
  input  C,
  input  [7:0] PCi,
  input  CO,
  input  J,
  output [7:0] DBG,
  output [7:0] PCo
);

  CounterPreset #(.Bits(4)) counterpreset_1 (
    .en(CE), .C(C), .dir(1'b0), .in(PCi[3:0]), .ld(J), .clr(1'b0), .out(DBG[3:0]));  // open: ovf
  assign PCo = CO ? {4'b0000, DBG[3:0]} : 8'bz;  // Driver driver_1

  assign DBG[7:4] = 4'b0000;

  // Notes on the sheet:
  //   CE: Count Enable: PC will count up on CLK rising edge when HIGH
  //   PCi: PC will be overwitten by this value if J is asserted. Used to jump to another instruction
  //   DBG: Debug Output
  //   CO: Value of PC is put on to bus when asserted
  //   J: Value to be loaded in to the Program Counter for Jump instructions
  //   PCo: Value of PC
endmodule
