// Digital circuit Reg.dig as structural Verilog
module Reg (
  input  [7:0] Di,
  input  LOAD,
  input  C,
  input  ENABLE,
  output [7:0] Du,
  output [7:0] Do
);

  Register #(.Bits(8), .generic("this.Bits=int(args.BusWidth);")) register_1 (.D(Di), .C(C), .en(LOAD), .Q(Du));
  assign Do = ENABLE ? Du : 8'bz;  // Driver driver_1

  // Notes on the sheet:
  //   Di: Data to be stored in Register. Data is stored when LOAD is LOW and rising edge of CLK
  //   LOAD: Data is saved in register from bus when this signal is asserted
  //   Du: Unbuffered output fot debugging
  //   ENABLE: Register data output to bus when this signal is asserted
  //   Do: The output
endmodule
